// Digital circuit adder-with-encoder.dig as structural Verilog
module adder_with_encoder (
  input  [31:0] A,
  input  [31:0] in_3,
  input  [31:0] in_4,
  input  [15:0] in_6,
  input  [15:0] in_7,
  input  [3:0] A_2,
  input  [1:0] in_10,
  input  [3:0] B_2,
  input  [3:0] C,
  input  [3:0] in_14,
  output [31:0] B,
  output [31:0] out_5,
  output [15:0] out_8,
  output [3:0] out_13
);

  wire [15:0] decoder_1_b, decoder_1_c;

  Add #(.Bits(32)) add_1 (.a(in_3), .b(in_4), .c_i(1'b0), .s(out_5));  // open: c_o
  Multiplexer #(.Bits(4), .Selector_Bits(2)) multiplexer_1 (
    .sel(in_10), .in_0(A_2), .in_1(B_2), .in_2(C), .in_3(in_14), .out(out_13));
  decoder decoder_1 (.A({in_7, in_6}), .C(decoder_1_c), .B(decoder_1_b));
  adder adder_1 (.A(decoder_1_c), .B(decoder_1_b), .result(out_8));
  // Pins of 1 and 4 bits meet at in_14

  assign B = A;
endmodule
