// Digital circuit adder-with-encoder.dig as structural Verilog
module adder_with_encoder (
  input  [31:0] A,
  input  [31:0] in_3,
  input  [31:0] in_4,
  input  [15:0] in_6,
  input  [15:0] in_7,
  output [31:0] B,
  output [31:0] out_5,
  output [15:0] out_8
);

  wire [15:0] decoder_1_b, decoder_1_c;

  Add #(.Bits(32)) add_1 (.a(in_3), .b(in_4), .c_i(1'b0), .s(out_5));  // open: c_o
  decoder decoder_1 (.A({in_7, in_6}), .C(decoder_1_c), .B(decoder_1_b));
  adder adder_1 (.A(decoder_1_c), .B(decoder_1_b), .result(out_8));

  assign B = A;
endmodule
