// Digital circuit frontpanel.dig as structural Verilog
module frontpanel (
  input  [15:0] in_1,
  input  [15:0] in_2,
  input  [3:0] A,
  input  [1:0] in_5,
  input  [3:0] B,
  input  [3:0] C,
  input  [3:0] in_9,
  output [15:0] out_3,
  output [3:0] out_8
);

  wire [15:0] decoder_1_b, decoder_1_c;

  Multiplexer #(.Selector_Bits(2), .Bits(4)) multiplexer_1 (
    .sel(in_5), .in_0(A), .in_1(B), .in_2(C), .in_3(in_9), .out(out_8));
  decoder decoder_1 (.A({in_2, in_1}), .C(decoder_1_c), .B(decoder_1_b));
  adder adder_1 (.A(decoder_1_c), .B(decoder_1_b), .result(out_3));
  // Pins of 1 and 4 bits meet at in_9
endmodule
