// Digital circuit frontpanel.dig as structural Verilog
module frontpanel (
  input  [15:0] in_1,
  input  [15:0] in_2,
  input  [15:0] in_3,
  input  [15:0] in_4,
  input  [15:0] in_5,
  input  [15:0] in_6,
  input  [15:0] in_7,
  input  [15:0] in_8,
  output [15:0] out_9,
  output [15:0] out_10,
  output [15:0] out_11,
  output [15:0] out_12
);

  wire button_1_out, demultiplexer_2_out_0, demultiplexer_2_out_1, demultiplexer_2_out_2,
       demultiplexer_2_out_3;
  wire [1:0] counter_1_out;
  wire [15:0] adder_1_result, decoder_1_b, decoder_1_c, demultiplexer_1_out_0, demultiplexer_1_out_1,
       demultiplexer_1_out_2, demultiplexer_1_out_3, multiplexer_2_out, multiplexer_3_out, multiplexer_4_out,
       multiplexer_5_out;
  wire [31:0] multiplexer_1_out;

  Counter #(.Bits(2)) counter_1 (.en(1'b1), .C(button_1_out), .clr(1'b0), .out(counter_1_out));  // open: ovf
  Button button_1 (.out(button_1_out));
  Multiplexer #(.Bits(32), .Selector_Bits(2)) multiplexer_1 (
    .sel(counter_1_out), .in_0({in_2, in_1}), .in_1({in_4, in_3}), .in_2({in_6, in_5}), .in_3({in_8, in_7}),
    .out(multiplexer_1_out));
  decoder decoder_1 (.A(multiplexer_1_out), .C(decoder_1_c), .B(decoder_1_b));
  adder adder_1 (.A(decoder_1_c), .B(decoder_1_b), .result(adder_1_result));
  Demultiplexer #(.Bits(16), .Selector_Bits(2)) demultiplexer_1 (
    .sel(counter_1_out), .in(adder_1_result), .out_0(demultiplexer_1_out_0), .out_1(demultiplexer_1_out_1),
    .out_2(demultiplexer_1_out_2), .out_3(demultiplexer_1_out_3));
  Demultiplexer #(.Selector_Bits(2)) demultiplexer_2 (
    .sel(counter_1_out), .in(1'b1), .out_0(demultiplexer_2_out_0), .out_1(demultiplexer_2_out_1),
    .out_2(demultiplexer_2_out_2), .out_3(demultiplexer_2_out_3));
  Multiplexer #(.Bits(16)) multiplexer_2 (
    .sel(demultiplexer_2_out_0), .in_0(out_9), .in_1(demultiplexer_1_out_0), .out(multiplexer_2_out));
  Multiplexer #(.Bits(16)) multiplexer_3 (
    .sel(demultiplexer_2_out_1), .in_0(out_10), .in_1(demultiplexer_1_out_1), .out(multiplexer_3_out));
  Multiplexer #(.Bits(16)) multiplexer_4 (
    .sel(demultiplexer_2_out_2), .in_0(out_11), .in_1(demultiplexer_1_out_2), .out(multiplexer_4_out));
  Multiplexer #(.Bits(16)) multiplexer_5 (
    .sel(demultiplexer_2_out_3), .in_0(out_12), .in_1(demultiplexer_1_out_3), .out(multiplexer_5_out));
  D_FF #(.Bits(16)) d_ff_1 (.D(multiplexer_2_out), .C(button_1_out), .Q(out_9));  // open: nQ
  D_FF #(.Bits(16)) d_ff_2 (.D(multiplexer_3_out), .C(button_1_out), .Q(out_10));  // open: nQ
  D_FF #(.Bits(16)) d_ff_3 (.D(multiplexer_4_out), .C(button_1_out), .Q(out_11));  // open: nQ
  D_FF #(.Bits(16)) d_ff_4 (.D(multiplexer_5_out), .C(button_1_out), .Q(out_12));  // open: nQ

  // Notes on the sheet:
  //   in_1: default 100
  //   in_2: default 32
  //   in_3: default 111
  //   in_4: default 36
  //   in_5: default 24
  //   in_6: default 52
  //   in_7: default 34
  //   in_8: default 21
endmodule
